// Digital circuit ALU.dig as structural Verilog
module ALU (
  input  [15:0] R0,
  input  [15:0] R1
);

  wire c_0, c_1, n_0, n_1, z_0, z_1;
  wire [15:0] not_1_out, result_2, result_3, result_4;
  wire [15:1] result_0, result_1;

  nand nand_1 (z_0, n_0, result_0[1], result_0[2], result_0[3], result_0[4], result_0[5], result_0[6], result_0[7], result_0[8], result_0[9], result_0[10], result_0[11], result_0[12], result_0[13], result_0[14], result_0[15]);
  Add #(.Bits(16)) add_1 (.a(R1), .b(R0), .c_i(1'b0), .s({result_0, n_0}), .c_o(c_0));
  nand nand_2 (z_1, n_1, result_1[1], result_1[2], result_1[3], result_1[4], result_1[5], result_1[6], result_1[7], result_1[8], result_1[9], result_1[10], result_1[11], result_1[12], result_1[13], result_1[14], result_1[15]);
  assign not_1_out = ~R1;  // Not not_1, 16 bits wide
  Add #(.Bits(16)) add_2 (.a(R0), .b(not_1_out), .c_i(1'b1), .s({result_1, n_1}), .c_o(c_1));
  assign result_2 = R0 & R1;  // And and_1, 16 bits wide
  assign result_3 = R1 | R0;  // Or or_1, 16 bits wide
  assign result_4 = ~R0;  // Not not_2, 16 bits wide

  // Other names for the same wires on the sheet: result_5[15:1] = R0[14:0]; result_6[14:0] = R0[15:1];
  //   result_0[0] = n_0; result_1[0] = n_1

  // Notes on the sheet:
  //   SUMA
  //   RESTA
  //   AND
  //   OR
  //   NOT
  //   LEFT BIT SHIFT
  //   RIGHT BIT SHIFT
endmodule
